# Fritzing sketch two_relays_one_switch (saved by Fritzing 0.9.6b)
perfboards: 1

parts:
  OMRON1 = OMRON PCB Power Relay – G5LE [part_number="G5LE-1\n" package=THT]
  J2 = Screw terminal - 2 pins [package=THT]
  J3 = Screw terminal - 2 pins [package=THT]
  HLK-PM1 = HLK-PM01
  OMRON2 = OMRON PCB Power Relay – G5LE [part_number="G5LE-1\n" package=THT]
  S2 = SPST Switch [package=switch-spdt_kit]
  Power_plug1 = Power plug

nets:
  N1: OMRON1.COIL1, HLK-PM1.+Vo, OMRON2.COIL1
  N2: OMRON1.C, J2.pin1
  N3: OMRON1.COIL2, OMRON2.COIL2, S2.P
  N4: OMRON1.B, HLK-PM1.AC#1, OMRON2.B, Power_plug1.VCC
  N5: J2.pin2, J3.pin2, HLK-PM1.AC#0, Power_plug1.GND
  N6: J3.pin1, OMRON2.C
  N7: HLK-PM1.-Vo, S2.S
